// Logisim project 124.circ as structural Verilog: 3 circuits, main circuit main
module main (
  input  CLEAR,
  input  in_2,
  input  in_3,
  input  in_4
);

  wire CLK;
  wire [3:0] rom_1_data;
  wire [15:0] A_q, adres_unit_1_adres_out, au_1_c, B_q, multiplexer_1_out, register_1_q;
  wire [15:4] rom_1_data_2;

  Clock clock_1 (.out(CLK));
  Register #(.width(16)) register_1 (.D(adres_unit_1_adres_out), .en(in_4), .Q(register_1_q), .clk(CLK), .clr(CLEAR));
  adres_unit adres_unit_1 (.ADRES_IN(register_1_q), .INSTRUCTION(rom_1_data), .ADRES_OUT(adres_unit_1_adres_out));
  Register #(.width(16)) A (.en(in_3), .Q(A_q), .clk(CLK), .clr(CLEAR));  // open: D
  Register #(.width(16)) B (.en(in_2), .Q(B_q), .clk(CLK), .clr(CLEAR));  // open: D
  ROM #(.addrWidth(16), .dataWidth(16)) rom_1 (.addr(register_1_q), .data({rom_1_data_2, rom_1_data}));  // open: sel
  AU au_1 (.A(A_q), .B(B_q), .EN(rom_1_data_2[15]), .Choise(rom_1_data_2[14:12]), .C(au_1_c));  // open: Cin, Cout
  Multiplexer #(.width(16)) multiplexer_1 (
    .in1(au_1_c), .out(multiplexer_1_out), .sel(rom_1_data_2[15]), .en(1'b1));  // open: in0
  Register #(.width(16)) A_2 (.D(multiplexer_1_out), .en(rom_1_data_2[15]), .clk(CLK), .clr(CLEAR));  // open: Q

  // Other names for the same wires on the sheet: EN_A = in_2; EN_B = in_3

  // Notes on the sheet:
  //   contents of rom_1 (hex, n*v repeats v):
  //   c002 b009 9001 d00a
endmodule

module AU (
  input  [15:0] A,
  input  [15:0] B,
  input  [15:0] Cin,
  input  EN,
  input  [2:0] Choise,
  output [15:0] C,
  output [15:0] Cout
);

  wire and_2_out;
  wire [0:0] adder_1_cout, subtractor_1_bout;
  wire [15:0] adder_1_out, and_1_out, divider_1_out, divider_1_rem, multiplier_1_cout, multiplier_1_out,
       not_1_out, or_1_out, subtractor_1_out, xor_1_out;

  assign not_1_out = ~A;  // NOT_Gate not_1, 16 bits wide
  assign and_1_out = A & B;  // AND_Gate and_1, 16 bits wide
  assign or_1_out = A | B;  // OR_Gate or_1, 16 bits wide
  assign xor_1_out = A ^ B;  // XOR_Gate xor_1, 16 bits wide
  Adder #(.width(16)) adder_1 (.a(A), .b(B), .out(adder_1_out), .cin(Cin[0]), .cout(adder_1_cout[0]));
  Subtractor #(.width(16)) subtractor_1 (
    .a(A), .b(B), .out(subtractor_1_out), .bin(Cin[0]), .bout(subtractor_1_bout[0]));
  Multiplier #(.width(16)) multiplier_1 (.a(A), .b(B), .out(multiplier_1_out), .cin(Cin), .cout(multiplier_1_cout));
  Divider #(.width(16)) divider_1 (.a(A), .b(B), .out(divider_1_out), .upper(Cin), .rem(divider_1_rem));
  Multiplexer #(.select(3), .width(16)) multiplexer_1 (
    .in0(not_1_out), .in1(and_1_out), .in2(or_1_out), .in3(xor_1_out), .in4(adder_1_out),
    .in5(subtractor_1_out), .in6(multiplier_1_out), .in7(divider_1_out), .out(C), .sel(Choise), .en(EN));
  and and_2 (and_2_out, Choise[2], EN);
  Multiplexer #(.select(2), .width(16)) multiplexer_2 (
    .in0({{15{1'b0}}, adder_1_cout[0]}), .in1({{15{1'b0}}, subtractor_1_bout[0]}), .in2(multiplier_1_cout),
    .in3(divider_1_rem), .out(Cout), .sel(Choise[1:0]), .en(and_2_out));
endmodule

module adres_unit (
  input  [15:0] ADRES_IN,
  input  [3:0] INSTRUCTION,
  output [15:0] ADRES_OUT
);

  wire [15:0] bit_extender_1_out, xor_1_out;

  assign bit_extender_1_out = {{13{1'b0}}, INSTRUCTION[2:0]};  // Bit_Extender bit_extender_1
  assign xor_1_out = bit_extender_1_out ^ {16{INSTRUCTION[3]}};  // XOR_Gate xor_1, 16 bits wide
  Adder #(.width(16)) adder_1 (.a(ADRES_IN), .b(xor_1_out), .out(ADRES_OUT), .cin(INSTRUCTION[3]));  // open: cout
endmodule
